# Fritzing sketch TerrariumRemote (saved by Fritzing 0.9.3b)
circuit board: 10.2768cm x 5.63466cm
breadboards: 1

parts:
  U2 = ESP8266 NodeMCU LoLin module
  Part1 = Adafruit 1.54inch 240x240 IPS TFT [part_number="Adafruit #3787"]
  S1 = Toggle Switch [package=THT]
  S2 = Toggle Switch [package=THT]
  LED1 = LED - 5mm [color="Red (633nm)" package="5 mm [THT]"]
  LED2 = LED - 5mm [color="Red (633nm)" package="5 mm [THT]"]
  R1 = Resistor [tolerance=±5% resistance=220 package=THT]
  R2 = Resistor [tolerance=±5% resistance=220 package=THT]

nets:
  N1: U2.D0, LED2.anode
  N2: U2.D1, Part1.TFTDC
  N3: U2.D2, Part1.TFTRST
  N4: U2.D3, LED1.anode
  3V3: U2.3V3, Part1.+3V3, S1.L2, S2.L2
  GND: U2.GND, Part1.GND, S1.L1, S2.L1, R1.Pin_0, R2.Pin_0
  N5: U2.D6, S1.COM
  N6: U2.D7, Part1.CARDCS
  N7: U2.D8, S2.COM
  N8: LED1.cathode, R1.Pin_1
  N9: LED2.cathode, R2.Pin_1

custom parts:
  ESP8266 NodeMCU LoLin module: ESP8266 based NodeMCU
  Adafruit 1.54inch 240x240 IPS TFT: We've been looking for a display like this for a long time - it's only 1.5" diagonal but has a high density 220 ppi, 240x240 pixel display with full-angle viewing. It looks a lot like our 1.44" 128x128 display, but has 4x as many pixels and looks great at any angle. We've seen displays of this caliber used in smartwatches and small electronic devices but they've always been MIPI interface.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
